# Fritzing sketch Constellaction PCB schema (saved by Fritzing 0.9.10b)
breadboards: 1

parts:
  Part1 = Arduino Uno (Rev3)
  J1 = Piezo Speaker
  R1 = PHOTOCELL [package=photocell]
  R2 = PHOTOCELL [package=photocell]
  R3 = PHOTOCELL [package=photocell]
  LED1 = smd LED [color="White (6500K)" package="1206 [SMD]"]
  LED2 = smd LED [color="White (6500K)" package="1206 [SMD]"]
  LED3 = smd LED [color="White (6500K)" package="1206 [SMD]"]
  Part2 = Adafruit Switched 20mm Coin Cell Breakout [part_number="Adafruit #1871"]
  R4 = Resistor [tolerance=±5% resistance=100k package="2010 [SMD]"]
  R5 = Resistor [tolerance=±5% resistance=100k package="2010 [SMD]"]
  R6 = Resistor [tolerance=±5% resistance=100k package="2010 [SMD]"]
  R7 = Resistor [tolerance=±5% resistance=220 package="2010 [SMD]"]
  R8 = Resistor [tolerance=±5% resistance=220 package="2010 [SMD]"]
  R9 = Resistor [tolerance=±5% resistance=220 package="2010 [SMD]"]
  R10 = Resistor [tolerance=±5% resistance=100 package="2010 [SMD]"]

nets:
  N1: Part1.A1, R3.P$1, R6.Pin_1
  N2: Part1.A2, R2.P$1, R5.Pin_1
  N3: Part1.A3, R1.P$1, R4.Pin_1
  N4: Part1.D8, LED1.anode
  N5: Part1.D9_PWM, R10.Pin_0
  N6: Part1.D10_PWM/SS, J1.pin2
  N7: Part1.D12/MISO, LED2.anode
  N8: Part1.D13/SCK, LED3.anode
  GND: Part1.GND, Part2.GND, R4.Pin_0, R5.Pin_0, R6.Pin_0, R7.Pin_1, R8.Pin_1, R9.Pin_1
  N9: Part1.3V3, R1.P$2, R2.P$2, R3.P$2, Part2.SW
  N10: J1.pin1, R10.Pin_1
  N11: LED1.cathode, R7.Pin_0
  N12: LED2.cathode, R8.Pin_0
  N13: LED3.cathode, R9.Pin_0

custom parts:
  Adafruit Switched 20mm Coin Cell Breakout: Simple but effective - this sewable breakout board has a CR2032 coin cell battery holder soldered on, an on/off switch and 0.1" pitch breakout pins for easy connecting. Great for powering very low-current projects, or adding a battery backup circuit to a real-time-clock or similar. There's two ground pins, one 'switched' power pin, and one pin that is always on.
